# Fritzing sketch Gavin_DPV_Nose (saved by Fritzing 0.9.3b)
circuit board: 5.56cm x 4.44cm
breadboards: 1

parts:
  Select = Pushbutton [package="[THT]"]
  BNO055 = 9-DOF Absolute Orientation IMU Fusion Breakout - BNO055
  TX/RX = female pin header, 2 pins [form="♀ (female)"]
  RST/Bttn = female pin header, 2 pins [form="♀ (female)"]
  VCC/GND = female pin header, 2 pins [form="♀ (female)"]
  SDA/SCL = female pin header, 2 pins [form="♀ (female)"]
  J1 = female pin header, 2 pins [form="♀ (female)"]
  SDA/TX = Dagu DGServo 9g header connector (female) [package=THT]
  RX/SCL = Dagu DGServo 9g header connector (female) [package=THT]
  Menu = OLED 0.96" 128x64 I2C SSD1306

nets:
  N1: Select.Pin_1, RST/Bttn.pin1
  GND: Select.Pin_3, Select.Pin_4, BNO055.GND, VCC/GND.pin1, Menu.GND
  N2: BNO055.5.0V, VCC/GND.pin2, J1.pin2, Menu.VCC
  N3: BNO055.SDA_5V, SDA/TX.Vcc
  N4: BNO055.SCL_5V, RX/SCL.Vcc
  N5: BNO055.RST_5V, RST/Bttn.pin2
  N6: BNO055.PS1_3V, J1.pin1
  N7: TX/RX.pin1, RX/SCL.gnd
  N8: TX/RX.pin2, SDA/TX.gnd
  N9: SDA/SCL.pin1, RX/SCL.pulse, Menu.SCL
  N10: SDA/SCL.pin2, SDA/TX.pulse, Menu.SCA

custom parts:
  9-DOF Absolute Orientation IMU Fusion Breakout - BNO055: A MEMS accelerometer, magnetometer and gyroscope on a single die with a high speed ARM Cortex-M0 based processor to digest all the sensor data, abstract the sensor fusion and real time requirements away, and spit out data you can use in quaternions, Euler angles or vectors.
